# Fritzing sketch schematics (saved by Fritzing 0.9.3b)
breadboards: 1

parts:
  Part1 = Arduino Uno (Rev3)
  S1 = Pushbutton [package="[THT]"]
  S2 = Pushbutton [package="[THT]"]
  LED1 = LED - 5mm [color="Red (633nm)" package="5 mm [THT]"]
  R2 = Resistor [tolerance=±5% resistance=220 package=THT]
  R3 = Resistor [tolerance=±5% resistance=220 package=THT]
  R1 = Resistor [tolerance=±5% resistance=220 package=THT]

nets:
  N1: Part1.D9_PWM, S2.Pin_1, S2.Pin_2, R2.Pin_0
  N2: Part1.D10_PWM/SS, S1.Pin_1, S1.Pin_2, R3.Pin_1
  N3: Part1.D7, R1.Pin_1
  N4: Part1.5V, R2.Pin_1, R3.Pin_0
  N5: Part1.GND, S1.Pin_3, S1.Pin_4, S2.Pin_3, S2.Pin_4, LED1.cathode
  N6: LED1.anode, R1.Pin_0
