# Fritzing sketch schematics (saved by Fritzing 0.9.3b)
breadboards: 1

parts:
  Part1 = Arduino Uno (Rev3)
  R1 = Resistor [tolerance=±5% resistance=10k package=THT]
  R2 = Resistor [tolerance=±5% resistance=1k package=THT]
  R3 = Resistor [tolerance=±5% resistance=10k package=THT]
  7_Segment1 = 7 Segment Display
  R4 = Photocell (LDR) [package=THT]
  Part2 = Thumb Joystick
  J1 = Basic Servo

nets:
  N1: Part1.A0, Part2.VERT
  N2: Part1.A1, Part2.HORZ
  GND: Part1.A5/SCL, Part1.GND, R4.pin_1, Part2.GND, J1.gnd
  N3: Part1.D8, 7_Segment1.Segment_F
  N4: Part1.D9_PWM, J1.pulse
  N5: Part1.D12/MISO, Part2.SEL
  N6: Part1.D2, 7_Segment1.Segment_A
  N7: Part1.D3_PWM, 7_Segment1.Segment_B
  N8: Part1.D4, 7_Segment1.Segment_C
  N9: Part1.D5_PWM, 7_Segment1.Segment_D
  N10: Part1.D6_PWM, 7_Segment1.Segment_E
  N11: Part1.D7, 7_Segment1.Segment_G
  VCC: Part1.5V, R1.Pin_0, R2.Pin_1, Part2.VCC, J1.vcc
  N12: R1.Pin_1, R3.Pin_0
  N13: R2.Pin_0, 7_Segment1.common_anode
  N14: R3.Pin_1, R4.pin_0
