# Fritzing sketch schematics (saved by Fritzing 0.9.3b)
breadboards: 1

parts:
  Part1 = Memoire 1.0 - SD card log shield
  Part2 = Arduino Uno (Rev3)  # not connected
  U1 = RF_RX
  U2 = CustomPart
  LED1 = RGB LED (com. cathode, rgb) [package="5 mm [THT]"]
  R1 = Resistor [tolerance=±5% resistance=1k package="0402 [SMD]"]

nets:
  N1: Part1.GND, U1.connector1, U2.connector2, R1.Pin_0
  N2: Part1.DIG_2, LED1.blue_anode
  N3: Part1.DIG_3, LED1.green_anode
  N4: Part1.DIG_4, LED1.red_anode
  N5: Part1.DIG_6, U2.connector1
  N6: Part1.DIG_7, U1.connector3
  N7: Part1.+5V, U1.connector4, U2.connector3
  N8: LED1.common_cathode, R1.Pin_1
