# Fritzing sketch schematics (saved by Fritzing 0.9.3b)
breadboards: 1

parts:
  U1 = CustomPart
  U2 = RF_RX
  Part1 = Arduino Uno (Rev3)
  Part2 = PIR D-SUN HC-SR501
  J1 = Basic Servo

nets:
  N1: U1.connector1, Part1.D6_PWM
  GND: U1.connector2, U2.connector1, Part1.GND, Part2.connector2, J1.gnd
  5V: U1.connector3, U2.connector4, Part1.5V, Part2.connector0, J1.vcc
  N2: U2.connector3, Part1.D7
  N3: Part1.D2, Part2.connector1
  N4: Part1.D3_PWM, J1.pulse
